# Fritzing sketch Security_Laser_Fritz_Sketch (saved by Fritzing 0.9.3b)
breadboards: 1

parts:
  Arduino_Mega_2560 = Arduino Mega 2560 (Rev3)
  LCD = LCD screen
  ldr1 = Photocell (LDR) [package=THT]
  ldr2 = Photocell (LDR) [package=THT]
  LED3 = smd LED [color="Green (570nm)" package="1206 [SMD]"]
  R4 = Resistor [tolerance=±5% resistance=150 package="1206 [SMD]"]
  R5 = Resistor [tolerance=±5% resistance=150 package="1206 [SMD]"]
  R6 = Resistor [tolerance=±5% resistance=150 package="1206 [SMD]"]
  LED4 = smd LED [color="Yellow (595nm)" package="1206 [SMD]"]
  LED6 = smd LED [color="Red (633nm)" package="0805 [SMD]"]
  Pot = POT [package=pot_mammoth]
  RFID-RC522 = RFID USB Reader
  S1 = Pushbutton [package="[THT]"]
  R7 = Resistor [tolerance=±5% resistance=10 package="0805 [SMD]"]
  R8 = Resistor [tolerance=±5% resistance=220 package="0805 [SMD]"]
  R9 = Resistor [tolerance=±5% resistance=220 package="0805 [SMD]"]
  R10 = Resistor [tolerance=±5% resistance=220 package="0805 [SMD]"]
  ldr3 = Photocell (LDR) [package=THT]
  laser2 = Photocell (LDR) [package=THT]
  laser3 = Photocell (LDR) [package=THT]
  laser1 = Photocell (LDR) [package=THT]
  J1 = Piezo Speaker

nets:
  N1: Arduino_Mega_2560.A0, ldr1.pin_0, R4.Pin_1
  N2: Arduino_Mega_2560.A2, ldr2.pin_0, R5.Pin_1
  N3: Arduino_Mega_2560.A3, R6.Pin_1, ldr3.pin_0
  N4: Arduino_Mega_2560.D12_PWM, LCD.RS
  N5: Arduino_Mega_2560.D11_PWM, LCD.E
  N6: Arduino_Mega_2560.D10_PWM, LCD.DB4
  N7: Arduino_Mega_2560.D9_PWM, LCD.DB5
  N8: Arduino_Mega_2560.D8_PWM, LCD.DB6
  3V3: Arduino_Mega_2560.3V3, RFID-RC522.VCC
  5V: Arduino_Mega_2560.5V, LCD.VDD, ldr1.pin_1, ldr2.pin_1, Pot.E, R7.Pin_1, ldr3.pin_1
  GND: Arduino_Mega_2560.GND, LCD.VSS, LCD.R/W, LCD.LED-, R4.Pin_0, R5.Pin_0, R6.Pin_0, Pot.S, RFID-RC522.TX-O, S1.Pin_1, S1.Pin_2, R8.Pin_0, R9.Pin_0, R10.Pin_0, laser2.pin_1, laser3.pin_1, laser1.pin_1, J1.pin1
  N9: Arduino_Mega_2560.D2_PWM, S1.Pin_3, S1.Pin_4
  N10: Arduino_Mega_2560.D7_PWM, LCD.DB7
  N11: Arduino_Mega_2560.D22, LED6.anode
  N12: Arduino_Mega_2560.D24, LED4.anode
  N13: Arduino_Mega_2560.D26, LED3.anode
  N14: Arduino_Mega_2560.D39, J1.pin2
  N15: Arduino_Mega_2560.D43, laser3.pin_0
  N16: Arduino_Mega_2560.D45, laser2.pin_0
  N17: Arduino_Mega_2560.D47, laser1.pin_0
  N18: Arduino_Mega_2560.D48, RFID-RC522.GND
  N19: Arduino_Mega_2560.D50, RFID-RC522.ANT1
  N20: Arduino_Mega_2560.D51, RFID-RC522.ANT2
  N21: Arduino_Mega_2560.D52, RFID-RC522.CP
  N22: Arduino_Mega_2560.D53, RFID-RC522.GNDT
  N23: LCD.V0, Pot.A
  N24: LCD.LED+, R7.Pin_0
  N25: LED3.cathode, R8.Pin_1
  N26: LED4.cathode, R10.Pin_1
  N27: LED6.cathode, R9.Pin_1

// code stored in the sketch: Arduino_fritz_code.ino
/*
 * SECURITY SYSTEM - RFID Based With Laser and LDR
 * Arduino Controlled System
*/

/*
 ************************************************************
 *----------------------LCD LIBRARY-------------------------*
 ************************************************************
*/
#include<LiquidCrystal.h>  // Including LCD Library
LiquidCrystal lcd(12, 11, 10, 9, 8, 7); //Configuring pins used 

/*
 ************************************************************
 *---------------------RFID LIBRARY-------------------------*
 ************************************************************
*/
#include <SPI.h> // Including SPI library which is used together with MFRC522 library
#include <MFRC522.h> //Including RC522 Library
 
#define SS_PIN 53 // Configuring SDA pin used
#define RST_PIN 48  // Configuring RST / RESET pin used
MFRC522 mfrc522(SS_PIN, RST_PIN);   // Create MFRC522 instance.

/*
 ************************************************************
 *-----------------CUSTOM DESIGN SYMBOL---------------------*
 ************************************************************
*/
// Designing a custom HEART Symbol ( Initialize the Function)
byte heart[8] = {
  0b00000,0b01010,0b11111,0b11111,0b11111,0b01110,0b00100,0b00000
};

// Designing a custom SMILEY Symbol ( Initialize the Function)
byte smiley[8] = { 
  0b00000,0b00000,0b01010,0b00000,0b00000,0b10001,0b01110,0b00000
};

// Designing a custom FROWNIE Symbol ( Initialize the Function)
byte frownie[8] = { 
  0b00000,0b00000,0b01010,0b00000,0b00000,0b00000,0b01110,0b10001
};

// Designing a custom ARMSDOWN Symbol ( Initialize the Function)
byte armsDown[8] = { 
  0b00100,0b01010,0b00100,0b00100,0b01110,0b10101,0b00100,0b01010
};

int redLed = 22;
int greenLed = 24;
int yellowLed = 26;

int alarm = 39;

int laser1 = 47;
int laser2 = 45;
int laser3 = 43;

//int resetButton = 2;

int resetBnState = 0;
//int resetBnState = LOW;

/*
 * ldr1 = A0;
 * ldr2 = A2;
 * ldr3 = A3;
*/

/*
 ************************************************************
 *----------------INITIALIZATION OF DATA--------------------*
 ************************************************************
*/
void setup() {
  lcd.begin(16,2);  // Initialize LCD
  lcd.createChar(1, heart); // Initializing the Symbol Creation Function in LCD
  lcd.createChar(2, smiley); // Initializing the Symbol Creation Function in LCD
  lcd.createChar(3, frownie); // Initializing the Symbol Creation Function in LCD
  lcd.createChar(4, armsDown); // Initializing the Symbol Creation Function in LCD
  
  SPI.begin();      // Initialize SPI bus
  mfrc522.PCD_Init();   // Initialize MFRC522
  mfrc522.PCD_DumpVersionToSerial();  // Show details of PCD - MFRC522 Card Reader details
  
  Serial.begin(9600);   // Initialize serial communications with the PC
  while (!Serial);    // Do nothing if no serial port is opened
  Serial.println(F("Scan PICC to see UID, SAK, type, and data blocks..."));

  pinMode(redLed, OUTPUT);
  pinMode(greenLed, OUTPUT);
  pinMode(yellowLed, OUTPUT);
  
  pinMode(alarm, OUTPUT);
  
  pinMode(laser1, OUTPUT);
  pinMode(laser2, OUTPUT);
  pinMode(laser3, OUTPUT);
  
          //lcd.write(1); // Print/Draw Heart symbol to the LCD
          //lcd.write(2); // Print/Draw Smiley symbol to the LCD
  lcd.clear();
  lcd.setCursor(0,0);
  lcd.write(1);lcd.write(1);lcd.write(2); 
  lcd.print(" SYSTEM ");
  lcd.write(2);lcd.write(1);lcd.write(1); 
  lcd.setCursor(2,1);
  lcd.write(2);lcd.write(2);
  lcd.print(" READY ");
  lcd.write(2);lcd.write(2);

  digitalWrite(greenLed, HIGH);

  digitalWrite(laser1, HIGH);
  digitalWrite(laser2, HIGH);
  digitalWrite(laser3, HIGH);

} //END SETUP()

/*
 ************************************************************
 *                                                          *
 *-----------------------MAIN CODE--------------------------*
 *                                                          *
 ************************************************************
*/

void loop() 
{
  // Scanning New Cards
  if ( ! mfrc522.PICC_IsNewCardPresent()) 
    {
      return;
    } //END IF() scanning cards
  // Selecting one of the Card
  if ( ! mfrc522.PICC_ReadCardSerial()) 
    {
      return;
    } //END IF() selecting cards
  
  //Show UID on serial monitor
  Serial.print("UID tag :");
  String content= ""; // Tag Name in Serial Monitor
  byte letter;
  for (byte i = 0; i < mfrc522.uid.size; i++) 
    {
       Serial.print(mfrc522.uid.uidByte[i] < 0x10 ? " 0" : " ");
       Serial.print(mfrc522.uid.uidByte[i], HEX); // Show UID as HEX code
       content.concat(String(mfrc522.uid.uidByte[i] < 0x10 ? " 0" : " "));
       content.concat(String(mfrc522.uid.uidByte[i], HEX)); // Show UID as HEX code
    } //END FOR()
  Serial.println();
  Serial.print("Message : ");
  content.toUpperCase(); // Display content in UpperCase

  if (analogRead(0) < 600)
  {
    digitalWrite(yellowLed,HIGH);
    
    lcd.clear();
    lcd.setCursor(0,0);
    lcd.print( "Scan Your Card" );
    delay(1000);

      if (content.substring(1) == "62 D9 EA D5") //UID of the card that will be given access
        {
          Serial.println("CARD 1");

          lcd.clear();
          lcd.setCursor(0,0);
          lcd.write(1); //Heart Symbol
          lcd.print(" WELCOME RONO ");
          lcd.write(1); //Heart Symbol
          delay(500);

          accessGranted();

          delay(1000);

          generalState();
          
        } //END IF() ** CARD 1
    
      else if (content.substring(1) == "A3 B7 8D 00") //UID of the card that will be given access
        {
          Serial.println("CARD 2");

          lcd.clear();
          lcd.setCursor(0,0);
          lcd.write(1); //Heart Symbol
          lcd.print(" WELCOME MARY ");
          lcd.write(1); //Heart Symbol
          delay(500);
          
          accessGranted();

          delay(1000);

          generalState();
          
          
        } //END ELSE IF() ** CARD 2
       
      else {
        Serial.println("CARD 3");
        accessDenied();
        
        delay(1000);

        generalState();
          
        
      } //END ELSE()
  } // END if (analogRead(0) < 600)

  if (analogRead(2) < 600 || analogRead(3) < 600 && analogRead(0) > 600 )
  {
    unauthorizedAccess();
    
    delay(1000);

    generalState();
          
    } //END if || ()
} //END VOID LOOP()

/*
 ************************************************************
 *                                                          *
 **********************CUSTOM FUNCTIONS**********************
 *                                                          *
 ************************************************************
*
------------------------------------------------------------------------------------------
------------------------------------------------------------------------------------------
/*
 ************************************************************
 *----------------ACCESS GRANTED FUNCTION-------------------*
 ************************************************************
*/

void accessGranted()
{
  digitalWrite(laser1, HIGH);
  digitalWrite(laser2, LOW);
  digitalWrite(laser3, LOW);

  digitalWrite(yellowLed, HIGH);
  digitalWrite(greenLed, LOW);
  digitalWrite(redLed, LOW);
  delay(2000);
  digitalWrite(yellowLed, LOW);
  
  lcd.setCursor(0,1);
  lcd.write(2); //Smiley Symbol
  lcd.print("ACCESS GRANTED");
  lcd.write(2); //Smiley Symbol

  delay(1000);
  } //END ACCESS GRANTED ()

/*
 ************************************************************
 *----------------ACCESS DENIED FUNCTION--------------------*
 ************************************************************
*/
void accessDenied()
{
  digitalWrite(laser1, HIGH);
  digitalWrite(laser2, HIGH);
  digitalWrite(laser3, HIGH);

  digitalWrite(yellowLed, LOW);
  digitalWrite(greenLed, LOW);
  digitalWrite(redLed, HIGH);
  digitalWrite(alarm, HIGH);
  delay(2000);
  digitalWrite(redLed, LOW);
  digitalWrite(alarm, LOW);
  
  lcd.clear();
  lcd.setCursor(0,0);
  lcd.write(3); //Frownie Symbol
  lcd.print(" UNAUTHORIZED ");
  lcd.write(3);
  
  lcd.setCursor(0,1);
  lcd.write(4); //ArmsDown Symbol
  lcd.print("ACCESS DENIED");
  lcd.write(4);

  delay(500);
  } //END ACCESS DENIED ()

/*
 ************************************************************
 *-------------UNAUTHORIZED ACCESS FUNCTION-----------------*
 ************************************************************
*/
void unauthorizedAccess()
{
  digitalWrite(laser1, HIGH);
  digitalWrite(laser2, HIGH);
  digitalWrite(laser3, HIGH);

  digitalWrite(redLed, HIGH);
  digitalWrite(alarm, HIGH);
  digitalWrite(yellowLed, LOW);
  digitalWrite(greenLed, LOW);
  delay(2000);
  digitalWrite(redLed, LOW);
  digitalWrite(alarm, LOW);
  
  lcd.setCursor(0,0);
  lcd.write(4); //ArmsDown Symbol
  lcd.print(" UNAUTHORIZED ");
  lcd.write(4); //ArmsDown Symbol

  lcd.setCursor(0,1);
  lcd.write(4);lcd.write(4);lcd.write(4); //ArmsDown Symbol
  lcd.print("  ACCESS  ");
  lcd.write(4);lcd.write(4);lcd.write(4); //ArmsDown Symbol

  delay(1000);
  } //END UNAUTHORIZED ACCESS ()
  
/*
 ************************************************************
 *----------------GENERAL STATE FUNCTION--------------------*
 ************************************************************
*/
void generalState() 
{
  digitalWrite(greenLed, HIGH);

  digitalWrite(laser1, HIGH);
  digitalWrite(laser2, HIGH);
  digitalWrite(laser3, HIGH);

  lcd.clear();
  lcd.setCursor(0,0);
  lcd.write(1);lcd.write(1);lcd.write(2); 
  lcd.print("  SYSTEM  ");
  lcd.write(2);lcd.write(1);lcd.write(1); 
  lcd.setCursor(2,1);
  lcd.write(2);lcd.write(2);
  lcd.print("  READY  ");
  lcd.write(2);lcd.write(2);

  delay(2000);

  lcd.clear();
  lcd.setCursor(0,0);
  lcd.write(1); 
  lcd.print(" SYSTEM READY ");
  lcd.write(1);
  symbolBlink();
  } //END GENERAL STATE ()

/*
 ************************************************************
 *----------------SYMBOL BLINK FUNCTION---------------------*
 ************************************************************
*/
void symbolBlink() 
  {
  lcd.setCursor(0,1); lcd.write(1); delay(500);
  lcd.setCursor(1, 1); lcd.write(2); delay(500);
  lcd.setCursor(2, 1); lcd.write(1); delay(500);
  lcd.setCursor(3, 1); lcd.write(2); delay(500);
  lcd.setCursor(4, 1); lcd.write(1); delay(500);
  lcd.setCursor(5, 1); lcd.write(2); delay(500);
  lcd.setCursor(6, 1); lcd.write(1); delay(500);
  lcd.setCursor(7, 1); lcd.write(2); delay(500);
  lcd.setCursor(8, 1); lcd.write(1); delay(500);
  lcd.setCursor(9, 1); lcd.write(2); delay(500);
  lcd.setCursor(10, 1); lcd.write(1); delay(500);
  lcd.setCursor(11, 1); lcd.write(2); delay(500);
  lcd.setCursor(12, 1); lcd.write(1); delay(500);
  lcd.setCursor(13, 1); lcd.write(2); delay(500);
  lcd.setCursor(14, 1); lcd.write(1); delay(500);
  lcd.setCursor(15, 1); lcd.write(2); delay(500);
  } //END SYMBOL BLINK ()
